# Fritzing sketch ltennis 89+ (saved by Fritzing 0.9.0b)
circuit board: 2.74235cm x 4.93204cm
perfboards: 1

parts:
  IC1 = Arduino Nano (Rev3.0)
  m3 = Basic Servo
  IC2 = L298 [part_number=SKU113918 package=l298n]
  M3 = DC Motor
  M2 = DC Motor
  J1 = screw terminal, 3 pins
  J2 = female pin header, 9 pins [form="♀ (female)"]

nets:
  GND: IC1.GND, m3.gnd, IC2.GND, J1.pin1, J2.pin8
  N1: IC1.D7, m3.pulse
  N2: IC1.D8, IC2.ENA, J2.pin6
  N3: IC1.D9, IC2.IN1, J2.pin5
  N4: IC1.D10, IC2.IN2, J2.pin4
  N5: IC1.D11/MOSI, IC2.IN3, J2.pin3
  N6: IC1.D12/MISO, IC2.IN4, J2.pin2
  5V: IC1.5V, m3.vcc, IC2.+5v, J1.pin2, J2.pin9
  N7: IC1.D13/SCK, IC2.ENB, J2.pin1
  12V: IC2.+12v, J1.pin3, J2.pin7
  N8: IC2.OUT1, M3.pin_2
  N9: IC2.OUT2, M3.pin_1
  N10: IC2.OUT3, M2.pin_2
  N11: IC2.OUT4, M2.pin_1

notes:
  pcb part: l928n connectoe
  ltennis 89+, 4

custom parts:
  L298: L298 Dual Full Bridge Driver
